// Logisim project auto_arm_proj.circ as structural Verilog: 3 circuits, main circuit auto_arm_simulation
module auto_arm_simulation (
);

  wire auto_arm_top_1_dest_blue_o, auto_arm_top_1_dest_init_o, auto_arm_top_1_dest_red_o,
       auto_arm_top_1_drop_o, auto_arm_top_1_move_o, auto_arm_top_1_scan_o, auto_arm_top_1_throw_o,
       clk_i_out, tclconsolereds_1_p23, tclconsolereds_1_p26;
  wire [1:0] tclconsolereds_1_p24;

  Clock clk_i (.out(clk_i_out));
  Clock sysclk ();  // open: out
  auto_arm_top auto_arm_top_1 (
    .ready_i(tclconsolereds_1_p23), .color_i(tclconsolereds_1_p24), .clk_i(clk_i_out),
    .reset_i(tclconsolereds_1_p26), .scan_o(auto_arm_top_1_scan_o), .throw_o(auto_arm_top_1_throw_o),
    .move_o(auto_arm_top_1_move_o), .dest_red_o(auto_arm_top_1_dest_red_o),
    .dest_blue_o(auto_arm_top_1_dest_blue_o), .dest_init_o(auto_arm_top_1_dest_init_o),
    .drop_o(auto_arm_top_1_drop_o));
  // TclConsoleReds #(.filePath("console\\console_auto_arm.tcl")) tclconsolereds_1: pin names not known; wires that end beside it: 4'b0000, 4'b0000, auto_arm_top_1_scan_o, auto_arm_top_1_throw_o, auto_arm_top_1_move_o, auto_arm_top_1_dest_red_o, auto_arm_top_1_dest_blue_o, auto_arm_top_1_dest_init_o, auto_arm_top_1_drop_o, 1'b0, 1'b0, 1'b0, 1'b0, 1'b0, 1'b0, 1'b0, 1'b0, 1'b0, {16{1'b0}}, {16{1'b0}}, {8{1'b0}}, clk_i_out, tclconsolereds_1_p23, tclconsolereds_1_p24[0], tclconsolereds_1_p24[1], tclconsolereds_1_p26

  // Notes on the sheet:
  //   Attention, votre version de Logisim
  //   ne contient pas de tracker. Si vous
  //   enregistrez votre projet, toutes les
  //   informations du tracker seront
  //   définitivement effacées.
endmodule

module auto_arm_top (
  input  ready_i,
  input  [1:0] color_i,
  input  clk_i,
  input  reset_i,
  output scan_o,
  output throw_o,
  output move_o,
  output dest_red_o,
  output dest_blue_o,
  output dest_init_o,
  output drop_o
);

  wire [6:0] register_1_q;

  Register #(.width(7)) register_1 (.D(7'b0000010), .clk(clk_i), .Q(register_1_q), .clr(reset_i));  // open: en
  Decodeur_de_sorties decodeur_de_sorties_1 (
    .input_i(register_1_q), .output_o({scan_o, throw_o, move_o, dest_red_o, dest_blue_o, dest_init_o, drop_o}));

  // Notes on the sheet:
  //   Attention, votre version de Logisim
  //   ne contient pas de tracker. Si vous
  //   enregistrez votre projet, toutes les
  //   informations du tracker seront
  //   définitivement effacées.
endmodule

module Decodeur_de_sorties (
  input  [6:0] input_i,
  output [6:0] output_o
);

  wire [6:0] multiplexer_1_out, multiplexer_2_out;

  Multiplexer #(.select(4), .width(7), .enable("false")) multiplexer_1 (
    .in0({7{1'b0}}), .in1({7{1'b0}}), .in2(7'b1000000), .in4(7'b0100000), .in8(7'b0010100),
    .out(multiplexer_1_out), .sel(input_i[3:0]));  // open: in3, in5, in6, in7, in9, in10, in11, in12, in13, in14, in15
  Multiplexer #(.select(3), .width(7), .enable("false")) multiplexer_2 (
    .in0({7{1'b0}}), .in1(7'b0011000), .in2(7'b0000001), .in4(7'b0010010), .out(multiplexer_2_out),
    .sel(input_i[6:4]));  // open: in3, in5, in6, in7
  assign output_o = multiplexer_1_out | multiplexer_2_out;  // OR_Gate or_1, 7 bits wide

  // Notes on the sheet:
  //   Attention, votre version de Logisim
  //   ne contient pas de tracker. Si vous
  //   enregistrez votre projet, toutes les
  //   informations du tracker seront
  //   définitivement effacées.
endmodule
